# Fritzing sketch PlantV1 (saved by Fritzing 0.9.8b)
breadboards: 1

parts:
  Part1 = Arduino Uno (Rev3)
  R1 = Photocell (LDR) [package=THT]
  R2 = Resistor [tolerance=±5% power=0.25 resistance=10k package=THT]
  R3 = Resistor [tolerance=±5% power=0.25 resistance=1M package=THT]
  R4 = Resistor [tolerance=±5% power=0.25 resistance=1k package=THT]

nets:
  N1: Part1.A0, R1.pin_1, R2.Pin_0
  N2: Part1.D2, R3.Pin_0
  N3: Part1.D3_PWM, R4.Pin_0
  N4: Part1.5V, R1.pin_0
  N5: Part1.GND, R2.Pin_1
  N6: R3.Pin_1, R4.Pin_1

notes:
  Capacitive Tape / Plant
